// Logisim project y86_processor.circ as structural Verilog: 15 circuits, main circuit main
module main (
  output [3:0] icode,
  output [63:0] valA,
  output [63:0] valE,
  output [63:0] valM,
  output [3:0] ifun,
  output [63:0] valB,
  output [3:0] ra,
  output [3:0] rb,
  output [63:0] valC,
  output [11:0] valP,
  output [2:0] OF_SF_ZF,
  output [3:0] destE,
  output [63:0] rax,
  output [3:0] destM,
  output [3:0] srcA,
  output [63:0] rcx,
  output [3:0] srcB,
  output [63:0] rdx,
  output [63:0] rbx,
  output [63:0] rsp,
  output [63:0] rbp,
  output [63:0] rsi,
  output [63:0] rdi,
  output [63:0] r8,
  output [63:0] r9,
  output [63:0] r10,
  output [63:0] r11,
  output [63:0] r12,
  output [63:0] r13,
  output [63:0] r14
);

  wire and_1_out, clock_1_out, comparator_1_eq, comparator_2_eq, comparator_2_gt, controlled_buffer_1_out,
       execute_1_cnd, not_1_out, not_2_out, not_3_out, or_1_out, pc_update_1_load, pc_update_1_reset;
  wire [7:0] Clock_Cycle_q;
  wire [11:0] pc_update_1_newpc, Program_Counter_q;

  Clock clock_1 (.out(clock_1_out));
  assign controlled_buffer_1_out = not_1_out ? clock_1_out : 1'bz;  // Controlled_Buffer controlled_buffer_1
  not not_1 (not_1_out, and_1_out);
  not not_2 (not_2_out, controlled_buffer_1_out);
  Counter #(.max('hfff), .width(12)) Program_Counter (
    .load(pc_update_1_load), .clk(not_2_out), .D(pc_update_1_newpc), .Q(Program_Counter_q));  // open: clr, up, count, carry
  Fetch fetch_1 (
    .pc(Program_Counter_q), .cyc(Clock_Cycle_q), .clk(controlled_buffer_1_out), .icode(icode), .ifun(ifun),
    .ra(ra), .rb(rb), .valC(valC), .valP(valP));
  Comparator #(.width(4)) comparator_1 (.a(icode), .b(4'b0000), .eq(comparator_1_eq));  // open: gt, lt
  Comparator comparator_2 (.a(Clock_Cycle_q), .b(8'h1), .gt(comparator_2_gt), .eq(comparator_2_eq));  // open: lt
  or or_1 (or_1_out, comparator_2_gt, comparator_2_eq);
  Counter Clock_Cycle (.clr(pc_update_1_reset), .clk(not_3_out), .Q(Clock_Cycle_q));  // open: load, up, count, D, carry
  not not_3 (not_3_out, controlled_buffer_1_out);
  and and_1 (and_1_out, comparator_1_eq, or_1_out);
  dst_and_src dst_and_src_1 (
    .cnd(execute_1_cnd), .icode(icode), .ra(ra), .rb(rb), .destE(destE), .destM(destM), .srcA(srcA),
    .srcB(srcB));
  register_file register_file_1 (
    .valE(valE), .valM(valM), .srcA(srcA), .destE(destE), .srcB(srcB), .destM(destM),
    .clk(controlled_buffer_1_out), .cyc(Clock_Cycle_q), .valA(valA), .valB(valB), .ax(rax), .cx(rcx),
    .dx(rdx), .bx(rbx), .sp(rsp), .bp(rbp), .si(rsi), .di(rdi), .eight(r8), .nine(r9), .ten(r10), .elev(r11),
    .twel(r12), .thirt(r13), .fourt(r14));
  Execute execute_1 (
    .icode(icode), .ifun(ifun), .valC(valC), .valA(valA), .valB(valB), .clk(controlled_buffer_1_out),
    .cyc(Clock_Cycle_q), .Cnd(execute_1_cnd), .valE(valE), .flags(OF_SF_ZF));
  Memory memory_1 (
    .icode(icode), .valE(valE), .valA(valA), .valP(valP), .clk(controlled_buffer_1_out), .cyc(Clock_Cycle_q),
    .valM(valM));
  pc_update pc_update_1 (
    .icode(icode), .cnd(execute_1_cnd), .valC(valC), .valP(valP), .valM(valM), .cyc(Clock_Cycle_q),
    .newPC(pc_update_1_newpc), .reset(pc_update_1_reset), .load(pc_update_1_load));

  // Notes on the sheet:
  //   1-10 Cycle (10 cycles)
  //   1 cycle for each byte of instruction
  //   Updates on edge from high to low
  //   First for read and second for write to registers
  //   11 and 22 Cycle (2 cycles)
  //   12 Cycle (1 cycles)
  //   To set the CC
  //   13-21 Cycle (9 cycles)
  //   1 cycle for each byte read/write. 1 cycle offset for reading
  //   To synchronize reseting cycles and updating pc
  //   23 and 24 Cycle (2 cycles)
endmodule

module Fetch (
  input  [11:0] pc,
  input  [7:0] cyc,
  input  clk,
  output [3:0] icode,
  output [3:0] ifun,
  output [3:0] ra,
  output [3:0] rb,
  output [63:0] valC,
  output [11:0] valP
);

  wire comparator_1_eq, comparator_2_eq, comparator_3_eq, comparator_4_eq, comparator_5_eq, comparator_6_eq,
       comparator_7_eq, comparator_8_eq, comparator_9_eq, comparator_10_eq, comparator_11_eq;
  wire [0:0] align_1_r;
  wire [3:3] align_1_i;
  wire [7:0] Instruction_Memory_data, register_1_q, register_2_q, register_3_q, register_4_q, register_5_q,
       register_6_q, register_7_q, register_8_q, register_9_q, register_10_q;
  wire [11:0] adder_1_out, adder_2_out, ini_pc_q;

  Comparator comparator_1 (.a(cyc), .b({8{1'b0}}), .eq(comparator_1_eq));  // open: gt, lt
  Register register_1 (.D(Instruction_Memory_data), .en(comparator_2_eq), .clk(clk), .Q(register_1_q));  // open: clr
  Comparator comparator_2 (.a({8{1'b0}}), .b(cyc), .eq(comparator_2_eq));  // open: gt, lt
  ROM #(.addrWidth(12)) Instruction_Memory (.addr(pc), .data(Instruction_Memory_data));
  Register register_2 (.D(Instruction_Memory_data), .en(comparator_3_eq), .clk(clk), .Q(register_2_q));  // open: clr
  Comparator comparator_3 (.a(8'h1), .b(cyc), .eq(comparator_3_eq));  // open: gt, lt
  Comparator comparator_4 (.a(8'h2), .b(cyc), .eq(comparator_4_eq));  // open: gt, lt
  Register register_3 (.D(Instruction_Memory_data), .en(comparator_4_eq), .clk(clk), .Q(register_3_q));  // open: clr
  Register #(.width(12)) ini_pc (.D(pc), .en(comparator_1_eq), .clk(clk), .Q(ini_pc_q));  // open: clr
  Register register_4 (.D(Instruction_Memory_data), .en(comparator_5_eq), .clk(clk), .Q(register_4_q));  // open: clr
  Comparator comparator_5 (.a(8'h3), .b(cyc), .eq(comparator_5_eq));  // open: gt, lt
  Register register_5 (.D(Instruction_Memory_data), .en(comparator_6_eq), .clk(clk), .Q(register_5_q));  // open: clr
  Comparator comparator_6 (.a(8'h4), .b(cyc), .eq(comparator_6_eq));  // open: gt, lt
  Comparator comparator_7 (.a(8'h5), .b(cyc), .eq(comparator_7_eq));  // open: gt, lt
  Adder #(.width(12)) adder_1 (.a(ini_pc_q), .b({{11{1'b0}}, align_1_r[0]}), .out(adder_1_out));  // open: cin, cout
  Register register_6 (.D(Instruction_Memory_data), .en(comparator_7_eq), .clk(clk), .Q(register_6_q));  // open: clr
  Adder #(.width(12)) adder_2 (.a(adder_1_out), .b(12'h1), .out(adder_2_out));  // open: cin, cout
  Register register_7 (.D(Instruction_Memory_data), .en(comparator_8_eq), .clk(clk), .Q(register_7_q));  // open: clr
  Comparator comparator_8 (.a(8'h6), .b(cyc), .eq(comparator_8_eq));  // open: gt, lt
  Adder #(.width(12)) adder_3 (.a(adder_2_out), .b({{8{1'b0}}, align_1_i[3], 3'b000}), .out(valP));  // open: cin, cout
  Register register_8 (.D(Instruction_Memory_data), .en(comparator_9_eq), .clk(clk), .Q(register_8_q));  // open: clr
  Comparator comparator_9 (.a(8'h7), .b(cyc), .eq(comparator_9_eq));  // open: gt, lt
  Register register_9 (.D(Instruction_Memory_data), .en(comparator_10_eq), .clk(clk), .Q(register_9_q));  // open: clr
  Comparator comparator_10 (.a(8'h8), .b(cyc), .eq(comparator_10_eq));  // open: gt, lt
  Register register_10 (.D(Instruction_Memory_data), .en(comparator_11_eq), .clk(clk), .Q(register_10_q));  // open: clr
  Comparator comparator_11 (.a(8'h9), .b(cyc), .eq(comparator_11_eq));  // open: gt, lt
  align align_1 (
    .byte1(register_1_q), .byte2(register_2_q), .byte3(register_3_q), .byte4(register_4_q),
    .byte5(register_5_q), .byte6(register_6_q), .byte7(register_7_q), .byte8(register_8_q),
    .byte9(register_9_q), .byte10(register_10_q), .icode(icode), .ifun(ifun), .ra(ra), .rb(rb), .valC(valC),
    .r(align_1_r[0]), .i(align_1_i[3]));

  // Notes on the sheet:
  //   contents of Instruction_Memory (hex, n*v repeats v):
  //   30 f4 0 2 6*0 a0 5f 20 45 30 f0 20 7*0 61 4 80 59 7*0 80 d0 7*0 30 f9 65 7*0 30 fa a6 7*ff 62 9a 30
  //   fb d2 7*0 30 fc 47 fb 6*ff 63 bc 0 30 f0 65 7*0 40 5 8*0 30 f0 17 7*0 40 5 f8 7*ff 30 f0 f9 7*ff 40
  //   5 f0 7*ff 30 f0 4e 7*0 40 5 e8 7*ff 20 50 30 f3 18 7*0 61 30 90 50 25 8*0 60 21 30 f8 8 7*0 61 85 20
  //   8 61 58 71 b8 7*0 90
endmodule

module align (
  input  [7:0] byte1,
  input  [7:0] byte2,
  input  [7:0] byte3,
  input  [7:0] byte4,
  input  [7:0] byte5,
  input  [7:0] byte6,
  input  [7:0] byte7,
  input  [7:0] byte8,
  input  [7:0] byte9,
  input  [7:0] byte10,
  output [3:0] icode,
  output [3:0] ifun,
  output [3:0] ra,
  output [3:0] rb,
  output [63:0] valC,
  output r,
  output i
);

  wire and_1_out, and_2_out, and_3_out, and_4_out, and_5_out, nand_1_out, nand_2_out, nand_3_out, nand_4_out,
       nand_5_out, not_1_out, not_2_out, not_3_out, not_4_out, not_5_out, not_6_out, not_7_out, not_8_out,
       not_9_out, not_10_out, not_11_out, not_12_out, not_13_out, not_14_out, not_15_out, not_16_out,
       not_17_out, not_18_out, not_19_out, not_20_out, not_21_out, not_22_out, not_23_out, not_24_out;

  not not_1 (not_1_out, byte1[4]);
  not not_2 (not_2_out, byte1[5]);
  not not_3 (not_3_out, byte1[6]);
  not not_4 (not_4_out, byte1[7]);
  not not_5 (not_5_out, byte1[5]);
  not not_6 (not_6_out, byte1[6]);
  not not_7 (not_7_out, byte1[7]);
  not not_8 (not_8_out, byte1[7]);
  not not_9 (not_9_out, byte1[4]);
  not not_10 (not_10_out, byte1[5]);
  not not_11 (not_11_out, byte1[6]);
  not not_12 (not_12_out, byte1[5]);
  not not_13 (not_13_out, byte1[6]);
  not not_14 (not_14_out, byte1[6]);
  not not_15 (not_15_out, byte1[7]);
  not not_16 (not_16_out, byte1[4]);
  not not_17 (not_17_out, byte1[5]);
  not not_18 (not_18_out, byte1[7]);
  not not_19 (not_19_out, byte1[5]);
  not not_20 (not_20_out, byte1[7]);
  not not_21 (not_21_out, byte1[7]);
  not not_22 (not_22_out, byte1[4]);
  not not_23 (not_23_out, byte1[5]);
  not not_24 (not_24_out, byte1[6]);
  nand nand_1 (nand_1_out, not_1_out, not_2_out, not_3_out, not_4_out);
  nand nand_2 (nand_2_out, byte1[4], not_5_out, not_6_out, not_7_out);
  nand nand_3 (nand_3_out, byte1[4], byte1[5], byte1[6], not_8_out);
  nand nand_4 (nand_4_out, not_9_out, not_10_out, not_11_out, byte1[7]);
  nand nand_5 (nand_5_out, byte1[4], not_12_out, not_13_out, byte1[7]);
  and and_1 (and_1_out, byte1[4], byte1[5], not_14_out, not_15_out);
  and and_2 (and_2_out, not_16_out, not_17_out, byte1[6], not_18_out);
  and and_3 (and_3_out, byte1[4], not_19_out, byte1[6], not_20_out);
  and and_4 (and_4_out, byte1[4], byte1[5], byte1[6], not_21_out);
  and and_5 (and_5_out, not_22_out, not_23_out, not_24_out, byte1[7]);
  and and_6 (r, nand_1_out, nand_2_out, nand_3_out, nand_4_out, nand_5_out);
  or or_1 (i, and_1_out, and_2_out, and_3_out, and_4_out, and_5_out);
  Multiplexer #(.width(4)) multiplexer_1 (.in0(4'b1111), .in1(byte2[7:4]), .out(ra), .sel(r));
  Multiplexer #(.width(4)) multiplexer_2 (.in0(4'b1111), .in1(byte2[3:0]), .out(rb), .sel(r));
  Multiplexer #(.width(64)) multiplexer_3 (
    .in0({byte9, byte8, byte7, byte6, byte5, byte4, byte3, byte2}),
    .in1({byte10, byte9, byte8, byte7, byte6, byte5, byte4, byte3}), .out(valC), .sel(r));

  assign icode = byte1[7:4];
  assign ifun = byte1[3:0];
endmodule

module dst_and_src (
  input  cnd,
  input  [3:0] icode,
  input  [3:0] ra,
  input  [3:0] rb,
  output [3:0] destE,
  output [3:0] destM,
  output [3:0] srcA,
  output [3:0] srcB
);

  wire and_1_out, comparator_1_eq, comparator_2_eq, comparator_3_eq, comparator_4_eq, comparator_5_eq,
       comparator_6_eq, comparator_7_eq, comparator_8_eq, comparator_9_eq, comparator_10_eq,
       comparator_11_eq, comparator_12_eq, comparator_13_eq, comparator_14_eq, comparator_15_eq,
       comparator_16_eq, comparator_17_eq, comparator_18_eq, comparator_19_eq, comparator_20_eq,
       comparator_21_eq, comparator_22_eq, comparator_23_eq, or_3_out;
  wire [1:0] or_1_out, or_4_out, or_6_out;

  Comparator #(.width(4)) comparator_1 (.a(icode), .b(4'b0110), .eq(comparator_1_eq));  // open: gt, lt
  Comparator #(.width(4)) comparator_2 (.a(icode), .b(4'b0011), .eq(comparator_2_eq));  // open: gt, lt
  Comparator #(.width(4)) comparator_3 (.a(icode), .b(4'b0010), .eq(comparator_3_eq));  // open: gt, lt
  Comparator #(.width(4)) comparator_4 (.a(icode), .b(4'b1000), .eq(comparator_4_eq));  // open: gt, lt
  Comparator #(.width(4)) comparator_5 (.a(icode), .b(4'b1001), .eq(comparator_5_eq));  // open: gt, lt
  Comparator #(.width(4)) comparator_6 (.a(icode), .b(4'b1010), .eq(comparator_6_eq));  // open: gt, lt
  Comparator #(.width(4)) comparator_7 (.a(icode), .b(4'b1011), .eq(comparator_7_eq));  // open: gt, lt
  Comparator #(.width(4)) comparator_8 (.a(icode), .b(4'b1011), .eq(comparator_8_eq));  // open: gt, lt
  Comparator #(.width(4)) comparator_9 (.a(icode), .b(4'b0101), .eq(comparator_9_eq));  // open: gt, lt
  Comparator #(.width(4)) comparator_10 (.a(icode), .b(4'b1011), .eq(comparator_10_eq));  // open: gt, lt
  Comparator #(.width(4)) comparator_11 (.a(icode), .b(4'b1001), .eq(comparator_11_eq));  // open: gt, lt
  Comparator #(.width(4)) comparator_12 (.a(icode), .b(4'b0010), .eq(comparator_12_eq));  // open: gt, lt
  Comparator #(.width(4)) comparator_13 (.a(icode), .b(4'b0100), .eq(comparator_13_eq));  // open: gt, lt
  Comparator #(.width(4)) comparator_14 (.a(icode), .b(4'b0110), .eq(comparator_14_eq));  // open: gt, lt
  Comparator #(.width(4)) comparator_15 (.a(icode), .b(4'b1010), .eq(comparator_15_eq));  // open: gt, lt
  Comparator #(.width(4)) comparator_16 (.a(icode), .b(4'b0011), .eq(comparator_16_eq));  // open: gt, lt
  Comparator #(.width(4)) comparator_17 (.a(icode), .b(4'b0100), .eq(comparator_17_eq));  // open: gt, lt
  Comparator #(.width(4)) comparator_18 (.a(icode), .b(4'b0101), .eq(comparator_18_eq));  // open: gt, lt
  Comparator #(.width(4)) comparator_19 (.a(icode), .b(4'b0110), .eq(comparator_19_eq));  // open: gt, lt
  Comparator #(.width(4)) comparator_20 (.a(icode), .b(4'b1000), .eq(comparator_20_eq));  // open: gt, lt
  Comparator #(.width(4)) comparator_21 (.a(icode), .b(4'b1001), .eq(comparator_21_eq));  // open: gt, lt
  Comparator #(.width(4)) comparator_22 (.a(icode), .b(4'b1010), .eq(comparator_22_eq));  // open: gt, lt
  Comparator #(.width(4)) comparator_23 (.a(icode), .b(4'b1011), .eq(comparator_23_eq));  // open: gt, lt
  or or_1 (or_1_out[0], comparator_1_eq, comparator_2_eq, and_1_out);
  and and_1 (and_1_out, comparator_3_eq, cnd);
  or or_2 (or_1_out[1], comparator_4_eq, comparator_5_eq, comparator_6_eq, comparator_7_eq);
  or or_3 (or_3_out, comparator_8_eq, comparator_9_eq);
  or or_4 (or_4_out[0], comparator_10_eq, comparator_11_eq);
  or or_5 (or_4_out[1], comparator_12_eq, comparator_13_eq, comparator_14_eq, comparator_15_eq);
  or or_6 (or_6_out[0], comparator_16_eq, comparator_17_eq, comparator_18_eq, comparator_19_eq);
  or or_7 (or_6_out[1], comparator_20_eq, comparator_21_eq, comparator_22_eq, comparator_23_eq);
  Multiplexer #(.select(2), .width(4)) multiplexer_1 (
    .in0(4'b1111), .in1(rb), .in2(4'b0100), .out(destE), .sel(or_1_out));  // open: in3
  Multiplexer #(.width(4)) multiplexer_2 (.in0(4'b1111), .in1(ra), .out(destM), .sel(or_3_out));
  Multiplexer #(.select(2), .width(4)) multiplexer_3 (
    .in0(4'b1111), .in1(4'b0100), .in2(ra), .out(srcA), .sel(or_4_out));  // open: in3
  Multiplexer #(.select(2), .width(4)) multiplexer_4 (
    .in0(4'b1111), .in1(rb), .in2(4'b0100), .out(srcB), .sel(or_6_out));  // open: in3
endmodule

module pc_update (
  input  [3:0] icode,
  input  cnd,
  input  [63:0] valC,
  input  [11:0] valP,
  input  [63:0] valM,
  input  [7:0] cyc,
  output [11:0] newPC,
  output reset,
  output load
);

  wire comparator_2_eq, comparator_2_gt;
  wire [11:0] multiplexer_1_out;

  Comparator comparator_1 (.a(cyc), .b(8'h17), .eq(reset));  // open: gt, lt
  Comparator comparator_2 (.a(cyc), .b(8'h16), .gt(comparator_2_gt), .eq(comparator_2_eq));  // open: lt
  Multiplexer #(.width(12)) multiplexer_1 (.in0(valP), .in1(valC[11:0]), .out(multiplexer_1_out), .sel(cnd));
  or or_1 (load, comparator_2_eq, comparator_2_gt);
  Multiplexer #(.select(4), .width(12)) multiplexer_2 (
    .in0(valP), .in1(valP), .in2(valP), .in3(valP), .in4(valP), .in5(valP), .in6(valP),
    .in7(multiplexer_1_out), .in8(valC[11:0]), .in9(valM[11:0]), .in10(valP), .in11(valP), .out(newPC),
    .sel(icode));  // open: in12, in13, in14, in15
endmodule

module a_alu (
  input  [3:0] icode,
  input  [63:0] valC,
  input  [63:0] valA,
  output [63:0] op1
);

  Multiplexer #(.select(4), .width(64)) multiplexer_1 (
    .in2(valA), .in3(valC), .in4(valC), .in5(valC), .in6(valA), .in8(64'hfffffffffffffff8), .in9(64'h8),
    .in10(64'hfffffffffffffff8), .in11(64'h8), .out(op1), .sel(icode));  // open: in0, in1, in7, in12, in13, in14, in15

  // Notes on the sheet:
  //   Constant Values
endmodule

module b_alu (
  input  [3:0] icode,
  input  [63:0] valB,
  output [63:0] op2
);

  Multiplexer #(.select(4), .width(64)) multiplexer_1 (
    .in2({64{1'b0}}), .in3({64{1'b0}}), .in4(valB), .in5(valB), .in6(valB), .in8(valB), .in9(valB),
    .in10(valB), .in11(valB), .out(op2), .sel(icode));  // open: in0, in1, in7, in12, in13, in14, in15
endmodule

module ifun_alu (
  input  [3:0] icode,
  input  [3:0] ifun,
  output [3:0] OP
);

  Multiplexer #(.select(4), .width(4)) multiplexer_1 (
    .in0(4'b0000), .in1(4'b0000), .in2(4'b0000), .in3(4'b0000), .in4(4'b0000), .in5(4'b0000), .in6(ifun),
    .in7(4'b0000), .in8(4'b0000), .in9(4'b0000), .in10(4'b0000), .in11(4'b0000), .out(OP), .sel(icode));  // open: in12, in13, in14, in15
endmodule

module CC (
  input  set_CC,
  input  [2:0] flags_input,
  input  clock,
  output [2:0] flags_output
);

  Register #(.width(1)) register_1 (.D(flags_input[0]), .en(set_CC), .clk(clock), .Q(flags_output[0]));  // open: clr
  Register #(.width(1)) register_2 (.D(flags_input[1]), .en(set_CC), .clk(clock), .Q(flags_output[1]));  // open: clr
  Register #(.width(1)) register_3 (.D(flags_input[2]), .en(set_CC), .clk(clock), .Q(flags_output[2]));  // open: clr

  // Notes on the sheet:
  //   ZF Register
  //   SF Register
  //   OF Register
endmodule

module ALU (
  input  [63:0] op1,
  input  [63:0] op2,
  input  [3:0] OP,
  output [63:0] valE,
  output [2:0] flags
);

  wire and_2_out, and_3_out, and_4_out, and_5_out, comparator_1_lt, comparator_2_lt, comparator_3_eq,
       comparator_4_lt, comparator_5_eq, comparator_6_eq, comparator_6_lt, multiplexer_2_out,
       multiplexer_3_out, multiplexer_4_out, not_1_out, not_2_out, not_3_out, not_4_out, not_5_out,
       not_6_out, not_7_out, or_1_out, or_2_out, xor_3_out;
  wire [63:0] adder_1_out, and_1_out, subtractor_1_out, xor_1_out;

  Adder #(.width(64)) adder_1 (.a(op1), .b(op2), .out(adder_1_out));  // open: cin, cout
  Subtractor #(.width(64)) subtractor_1 (.a(op2), .b(op1), .out(subtractor_1_out));  // open: bin, bout
  Comparator #(.width(64)) comparator_1 (.a(op1), .b({64{1'b0}}), .lt(comparator_1_lt));  // open: gt, eq
  Comparator #(.width(64)) comparator_2 (.a(op2), .b({64{1'b0}}), .lt(comparator_2_lt));  // open: gt, eq
  assign and_1_out = op1 & op2;  // AND_Gate and_1, 64 bits wide
  assign xor_1_out = op1 ^ op2;  // XOR_Gate xor_1, 64 bits wide
  Multiplexer #(.select(4), .width(64)) multiplexer_1 (
    .in0(adder_1_out), .in1(subtractor_1_out), .in2(and_1_out), .in3(xor_1_out), .in4(adder_1_out),
    .out(valE), .sel(OP));  // open: in5, in6, in7, in8, in9, in10, in11, in12, in13, in14, in15
  Comparator #(.width(1)) comparator_3 (
    .a(comparator_1_lt), .b(comparator_2_lt), .eq(comparator_3_eq));  // open: gt, lt
  Comparator #(.width(1)) comparator_4 (.gt(comparator_3_eq), .lt(comparator_4_lt));  // open: a, b, eq
  xor xor_2 (comparator_4_lt, comparator_1_lt, comparator_6_lt);
  xor xor_3 (xor_3_out, comparator_2_lt, comparator_1_lt);
  Comparator #(.width(1)) comparator_5 (
    .a(comparator_1_lt), .b(comparator_6_lt), .eq(comparator_5_eq));  // open: gt, lt
  and and_2 (and_2_out, comparator_3_eq, and_4_out, comparator_4_lt);
  and and_3 (and_3_out, xor_3_out, and_5_out, comparator_5_eq);
  not not_1 (not_1_out, OP[0]);
  not not_2 (not_2_out, OP[1]);
  not not_3 (not_3_out, OP[2]);
  not not_4 (not_4_out, OP[3]);
  not not_5 (not_5_out, OP[1]);
  not not_6 (not_6_out, OP[2]);
  not not_7 (not_7_out, OP[3]);
  Comparator #(.width(64)) comparator_6 (
    .a(valE), .b({64{1'b0}}), .eq(comparator_6_eq), .lt(comparator_6_lt));  // open: gt
  and and_4 (and_4_out, not_1_out, not_2_out, not_3_out, not_4_out);
  or or_1 (or_1_out, and_4_out, and_5_out);
  and and_5 (and_5_out, OP[0], not_5_out, not_6_out, not_7_out);
  Multiplexer multiplexer_2 (.in0(1'b0), .in1(1'b1), .out(multiplexer_2_out), .sel(comparator_6_eq));
  Multiplexer multiplexer_3 (.in0(1'b0), .in1(1'b1), .out(multiplexer_3_out), .sel(comparator_6_lt));
  Multiplexer multiplexer_4 (.in0(1'b0), .in1(1'b1), .out(multiplexer_4_out), .sel(or_2_out));
  or or_2 (or_2_out, and_2_out, and_3_out);
  buf and_6 (flags[0], multiplexer_2_out);  // AND_Gate
  buf and_7 (flags[1], multiplexer_3_out);  // AND_Gate
  and and_8 (flags[2], or_1_out, multiplexer_4_out);

  // Notes on the sheet:
  //   a<0
  //   b<0
  //   OF-SF-ZF
endmodule

module COND (
  input  [3:0] ifun,
  input  [2:0] flags_input,
  output Cnd
);

  wire and_1_out, not_1_out, not_2_out, not_3_out, or_1_out, xor_1_out;

  xor xor_1 (xor_1_out, flags_input[1], flags_input[2]);
  or or_1 (or_1_out, flags_input[0], xor_1_out);
  not not_1 (not_1_out, xor_1_out);
  not not_2 (not_2_out, flags_input[0]);
  not not_3 (not_3_out, flags_input[0]);
  and and_1 (and_1_out, not_1_out, not_2_out);
  Multiplexer #(.select(4)) multiplexer_1 (
    .in0(1'b1), .in1(or_1_out), .in2(xor_1_out), .in3(flags_input[0]), .in4(not_3_out), .in5(not_1_out),
    .in6(and_1_out), .out(Cnd), .sel(ifun));  // open: in7, in8, in9, in10, in11, in12, in13, in14, in15

  // Notes on the sheet:
  //   O-S-Z
endmodule

module SET_CC (
  input  [3:0] icode,
  output CC
);

  Multiplexer #(.select(4)) multiplexer_1 (
    .in0(1'b0), .in1(1'b0), .in2(1'b0), .in3(1'b0), .in4(1'b0), .in5(1'b0), .in6(1'b1), .in7(1'b0),
    .in8(1'b0), .in9(1'b0), .in10(1'b0), .in11(1'b0), .out(CC), .sel(icode));  // open: in12, in13, in14, in15
endmodule

module Execute (
  input  [3:0] icode,
  input  [3:0] ifun,
  input  [63:0] valC,
  input  [63:0] valA,
  input  [63:0] valB,
  input  clk,
  input  [7:0] cyc,
  output Cnd,
  output [63:0] valE,
  output [2:0] flags
);

  wire and_1_out, comparator_1_eq, set_cc_1_cc;
  wire [2:0] alu_1_flags;
  wire [3:0] ifun_alu_1_op;
  wire [63:0] a_alu_1_op1, b_alu_1_op2;

  Comparator comparator_1 (.a(cyc), .b(8'hb), .eq(comparator_1_eq));  // open: gt, lt
  SET_CC set_cc_1 (.icode(icode), .CC(set_cc_1_cc));
  a_alu a_alu_1 (.icode(icode), .valC(valC), .valA(valA), .op1(a_alu_1_op1));
  b_alu b_alu_1 (.icode(icode), .valB(valB), .op2(b_alu_1_op2));
  ifun_alu ifun_alu_1 (.icode(icode), .ifun(ifun), .OP(ifun_alu_1_op));
  and and_1 (and_1_out, set_cc_1_cc, comparator_1_eq);
  CC cc_1 (.set_CC(and_1_out), .flags_input(alu_1_flags), .clock(clk), .flags_output(flags));
  ALU alu_1 (.op1(a_alu_1_op1), .op2(b_alu_1_op2), .OP(ifun_alu_1_op), .valE(valE), .flags(alu_1_flags));
  COND cond_1 (.ifun(ifun), .flags_input(flags), .Cnd(Cnd));
endmodule

module register_file (
  input  [63:0] valE,
  input  [63:0] valM,
  input  [3:0] srcA,
  input  [3:0] destE,
  input  [3:0] srcB,
  input  [3:0] destM,
  input  clk,
  input  [7:0] cyc,
  output [63:0] valA,
  output [63:0] valB,
  output [63:0] ax,
  output [63:0] cx,
  output [63:0] dx,
  output [63:0] bx,
  output [63:0] sp,
  output [63:0] bp,
  output [63:0] si,
  output [63:0] di,
  output [63:0] eight,
  output [63:0] nine,
  output [63:0] ten,
  output [63:0] elev,
  output [63:0] twel,
  output [63:0] thirt,
  output [63:0] fourt
);

  wire and_1_out, and_2_out, and_3_out, and_4_out, and_5_out, and_6_out, and_7_out, and_8_out, and_9_out,
       and_10_out, and_11_out, and_12_out, and_13_out, and_14_out, and_15_out, and_16_out, comparator_1_eq,
       comparator_2_eq, comparator_3_eq, comparator_4_eq, comparator_5_eq, comparator_6_eq, comparator_7_eq,
       comparator_8_eq, comparator_9_eq, comparator_10_eq, comparator_11_eq, comparator_12_eq,
       comparator_13_eq, comparator_14_eq, comparator_15_eq, comparator_16_eq, comparator_17_eq,
       comparator_18_eq, comparator_19_eq, comparator_20_eq, comparator_21_eq, comparator_22_eq,
       comparator_23_eq, comparator_24_eq, comparator_25_eq, comparator_26_eq, comparator_27_eq,
       comparator_28_eq, comparator_29_eq, comparator_30_eq, comparator_31_eq, comparator_32_eq,
       comparator_33_eq, comparator_34_eq, comparator_35_eq, comparator_36_eq, comparator_37_eq,
       comparator_38_eq, comparator_39_eq, comparator_40_eq, comparator_41_eq, comparator_42_eq,
       comparator_43_eq, comparator_44_eq, comparator_45_eq, comparator_46_eq, comparator_47_eq,
       comparator_48_eq, comparator_49_eq, comparator_50_eq, comparator_51_eq, comparator_52_eq,
       comparator_53_eq, comparator_54_eq, comparator_55_eq, comparator_56_eq, comparator_57_eq,
       comparator_58_eq, comparator_59_eq, comparator_60_eq, comparator_61_eq, comparator_62_eq,
       comparator_63_eq, comparator_64_eq, comparator_65_eq, comparator_66_eq, comparator_67_eq,
       comparator_68_eq, controlled_buffer_33_out, controlled_buffer_34_out, not_1_out, not_2_out, not_3_out,
       not_4_out, not_5_out, or_1_out, or_2_out, or_3_out, or_4_out, or_5_out, or_6_out, or_7_out, or_8_out,
       or_9_out, or_10_out, or_11_out, or_12_out, or_13_out, or_14_out, or_15_out;
  wire [63:0] controlled_buffer_1_out, controlled_buffer_3_out, controlled_buffer_11_out, multiplexer_1_out,
       multiplexer_2_out, multiplexer_3_out, multiplexer_4_out, multiplexer_5_out, multiplexer_6_out,
       multiplexer_7_out, multiplexer_8_out, multiplexer_9_out, multiplexer_10_out, multiplexer_11_out,
       multiplexer_12_out, multiplexer_13_out, multiplexer_14_out, multiplexer_15_out;

  not not_1 (not_1_out, comparator_4_eq);
  Comparator #(.width(4)) comparator_1 (.a(destE), .b(4'b1111), .eq(comparator_1_eq));  // open: gt, lt
  Comparator #(.width(4)) comparator_2 (.a(destE), .b(4'b0100), .eq(comparator_2_eq));  // open: gt, lt
  and and_1 (and_1_out, comparator_2_eq, not_1_out);
  Comparator #(.width(4)) comparator_3 (.a(destM), .b(4'b1111), .eq(comparator_3_eq));  // open: gt, lt
  Comparator #(.width(4)) comparator_4 (.a(destM), .b(4'b1111), .eq(comparator_4_eq));  // open: gt, lt
  Comparator #(.width(4)) comparator_5 (.a(destE), .b(4'b0000), .eq(comparator_5_eq));  // open: gt, lt
  Comparator #(.width(4)) comparator_6 (.a(destE), .b(4'b0001), .eq(comparator_6_eq));  // open: gt, lt
  Comparator #(.width(4)) comparator_7 (.a(destE), .b(4'b0010), .eq(comparator_7_eq));  // open: gt, lt
  Comparator #(.width(4)) comparator_8 (.a(destE), .b(4'b0011), .eq(comparator_8_eq));  // open: gt, lt
  Comparator #(.width(4)) comparator_9 (.a(destM), .b(4'b0000), .eq(comparator_9_eq));  // open: gt, lt
  Comparator #(.width(4)) comparator_10 (.a(destM), .b(4'b0001), .eq(comparator_10_eq));  // open: gt, lt
  Comparator #(.width(4)) comparator_11 (.a(destM), .b(4'b0010), .eq(comparator_11_eq));  // open: gt, lt
  Comparator #(.width(4)) comparator_12 (.a(destM), .b(4'b0011), .eq(comparator_12_eq));  // open: gt, lt
  not not_2 (not_2_out, comparator_3_eq);
  not not_3 (not_3_out, comparator_1_eq);
  Comparator #(.width(4)) comparator_13 (.a(destE), .b(4'b0100), .eq(comparator_13_eq));  // open: gt, lt
  Comparator #(.width(4)) comparator_14 (.a(destE), .b(4'b0101), .eq(comparator_14_eq));  // open: gt, lt
  Comparator #(.width(4)) comparator_15 (.a(destE), .b(4'b0110), .eq(comparator_15_eq));  // open: gt, lt
  Comparator #(.width(4)) comparator_16 (.a(destE), .b(4'b0111), .eq(comparator_16_eq));  // open: gt, lt
  Comparator #(.width(4)) comparator_17 (.a(destM), .b(4'b0100), .eq(comparator_17_eq));  // open: gt, lt
  Comparator #(.width(4)) comparator_18 (.a(destM), .b(4'b0101), .eq(comparator_18_eq));  // open: gt, lt
  Comparator #(.width(4)) comparator_19 (.a(destM), .b(4'b0110), .eq(comparator_19_eq));  // open: gt, lt
  Comparator #(.width(4)) comparator_20 (.a(destM), .b(4'b0111), .eq(comparator_20_eq));  // open: gt, lt
  Comparator #(.width(4)) comparator_21 (.a(destE), .b(4'b1000), .eq(comparator_21_eq));  // open: gt, lt
  Comparator #(.width(4)) comparator_22 (.a(destE), .b(4'b1001), .eq(comparator_22_eq));  // open: gt, lt
  Comparator #(.width(4)) comparator_23 (.a(destE), .b(4'b1010), .eq(comparator_23_eq));  // open: gt, lt
  Comparator #(.width(4)) comparator_24 (.a(destE), .b(4'b1011), .eq(comparator_24_eq));  // open: gt, lt
  Comparator #(.width(4)) comparator_25 (.a(destM), .b(4'b1000), .eq(comparator_25_eq));  // open: gt, lt
  Comparator #(.width(4)) comparator_26 (.a(destM), .b(4'b1001), .eq(comparator_26_eq));  // open: gt, lt
  Comparator #(.width(4)) comparator_27 (.a(destM), .b(4'b1010), .eq(comparator_27_eq));  // open: gt, lt
  Comparator #(.width(4)) comparator_28 (.a(destM), .b(4'b1011), .eq(comparator_28_eq));  // open: gt, lt
  assign controlled_buffer_1_out = not_3_out ? valE : 64'bz;  // Controlled_Buffer controlled_buffer_1
  assign controlled_buffer_1_out = not_2_out ? valM : 64'bz;  // Controlled_Buffer controlled_buffer_2
  Comparator #(.width(4)) comparator_29 (.a(destE), .b(4'b1100), .eq(comparator_29_eq));  // open: gt, lt
  Comparator #(.width(4)) comparator_30 (.a(destE), .b(4'b1101), .eq(comparator_30_eq));  // open: gt, lt
  Comparator #(.width(4)) comparator_31 (.a(destE), .b(4'b1110), .eq(comparator_31_eq));  // open: gt, lt
  Comparator #(.width(4)) comparator_32 (.a(destM), .b(4'b1100), .eq(comparator_32_eq));  // open: gt, lt
  Comparator #(.width(4)) comparator_33 (.a(destM), .b(4'b1101), .eq(comparator_33_eq));  // open: gt, lt
  Comparator #(.width(4)) comparator_34 (.a(destM), .b(4'b1110), .eq(comparator_34_eq));  // open: gt, lt
  or or_1 (or_1_out, comparator_5_eq, comparator_9_eq);
  or or_2 (or_2_out, comparator_6_eq, comparator_10_eq);
  or or_3 (or_3_out, comparator_7_eq, comparator_11_eq);
  or or_4 (or_4_out, comparator_8_eq, comparator_12_eq);
  or or_5 (or_5_out, comparator_13_eq, comparator_17_eq);
  or or_6 (or_6_out, comparator_14_eq, comparator_18_eq);
  or or_7 (or_7_out, comparator_15_eq, comparator_19_eq);
  or or_8 (or_8_out, comparator_16_eq, comparator_20_eq);
  or or_9 (or_9_out, comparator_21_eq, comparator_25_eq);
  or or_10 (or_10_out, comparator_22_eq, comparator_26_eq);
  or or_11 (or_11_out, comparator_23_eq, comparator_27_eq);
  or or_12 (or_12_out, comparator_24_eq, comparator_28_eq);
  or or_13 (or_13_out, comparator_29_eq, comparator_32_eq);
  or or_14 (or_14_out, comparator_30_eq, comparator_33_eq);
  or or_15 (or_15_out, comparator_31_eq, comparator_34_eq);
  Comparator comparator_35 (.a(cyc), .b(8'h15), .eq(comparator_35_eq));  // open: gt, lt
  and and_2 (and_2_out, or_1_out, comparator_35_eq);
  and and_3 (and_3_out, or_2_out, comparator_35_eq);
  and and_4 (and_4_out, or_3_out, comparator_35_eq);
  and and_5 (and_5_out, or_4_out, comparator_35_eq);
  and and_6 (and_6_out, or_5_out, comparator_35_eq);
  and and_7 (and_7_out, or_6_out, comparator_35_eq);
  and and_8 (and_8_out, or_7_out, comparator_35_eq);
  and and_9 (and_9_out, or_8_out, comparator_35_eq);
  Register #(.width(64)) rax (.D(multiplexer_1_out), .en(and_2_out), .clk(clk), .Q(ax));  // open: clr
  Multiplexer #(.width(64)) multiplexer_1 (
    .in0(controlled_buffer_1_out), .in1(valM), .out(multiplexer_1_out), .sel(and_1_out));
  Register #(.width(64)) rcx (.D(multiplexer_2_out), .en(and_3_out), .clk(clk), .Q(cx));  // open: clr
  Multiplexer #(.width(64)) multiplexer_2 (
    .in0(controlled_buffer_1_out), .in1(valM), .out(multiplexer_2_out), .sel(and_1_out));
  Register #(.width(64)) rdx (.D(multiplexer_3_out), .en(and_4_out), .clk(clk), .Q(dx));  // open: clr
  Multiplexer #(.width(64)) multiplexer_3 (
    .in0(controlled_buffer_1_out), .in1(valM), .out(multiplexer_3_out), .sel(and_1_out));
  Register #(.width(64)) rbx (.D(multiplexer_4_out), .en(and_5_out), .clk(clk), .Q(bx));  // open: clr
  Multiplexer #(.width(64)) multiplexer_4 (
    .in0(controlled_buffer_1_out), .in1(valM), .out(multiplexer_4_out), .sel(and_1_out));
  Register #(.width(64)) rsp (.D(multiplexer_5_out), .en(and_6_out), .clk(clk), .Q(sp));  // open: clr
  Multiplexer #(.width(64)) multiplexer_5 (
    .in0(controlled_buffer_1_out), .in1(valE), .out(multiplexer_5_out), .sel(and_1_out));
  Register #(.width(64)) rbp (.D(multiplexer_6_out), .en(and_7_out), .clk(clk), .Q(bp));  // open: clr
  Multiplexer #(.width(64)) multiplexer_6 (
    .in0(controlled_buffer_1_out), .in1(valM), .out(multiplexer_6_out), .sel(and_1_out));
  Register #(.width(64)) rsi (.D(multiplexer_7_out), .en(and_8_out), .clk(clk), .Q(si));  // open: clr
  Multiplexer #(.width(64)) multiplexer_7 (
    .in0(controlled_buffer_1_out), .in1(valM), .out(multiplexer_7_out), .sel(and_1_out));
  Register #(.width(64)) rdi (.D(multiplexer_8_out), .en(and_9_out), .clk(clk), .Q(di));  // open: clr
  Multiplexer #(.width(64)) multiplexer_8 (
    .in0(controlled_buffer_1_out), .in1(valM), .out(multiplexer_8_out), .sel(and_1_out));
  Comparator comparator_36 (.a(cyc), .b(8'ha), .eq(comparator_36_eq));  // open: gt, lt
  assign controlled_buffer_3_out = comparator_39_eq ? ax : 64'bz;  // Controlled_Buffer controlled_buffer_3
  assign controlled_buffer_3_out = comparator_40_eq ? cx : 64'bz;  // Controlled_Buffer controlled_buffer_4
  assign controlled_buffer_3_out = comparator_41_eq ? dx : 64'bz;  // Controlled_Buffer controlled_buffer_5
  assign controlled_buffer_3_out = comparator_42_eq ? bx : 64'bz;  // Controlled_Buffer controlled_buffer_6
  assign controlled_buffer_3_out = comparator_47_eq ? sp : 64'bz;  // Controlled_Buffer controlled_buffer_7
  assign controlled_buffer_3_out = comparator_48_eq ? bp : 64'bz;  // Controlled_Buffer controlled_buffer_8
  assign controlled_buffer_3_out = comparator_49_eq ? si : 64'bz;  // Controlled_Buffer controlled_buffer_9
  assign controlled_buffer_3_out = comparator_50_eq ? di : 64'bz;  // Controlled_Buffer controlled_buffer_10
  assign controlled_buffer_11_out = comparator_43_eq ? ax : 64'bz;  // Controlled_Buffer controlled_buffer_11
  assign controlled_buffer_11_out = comparator_44_eq ? cx : 64'bz;  // Controlled_Buffer controlled_buffer_12
  assign controlled_buffer_11_out = comparator_45_eq ? dx : 64'bz;  // Controlled_Buffer controlled_buffer_13
  assign controlled_buffer_11_out = comparator_46_eq ? bx : 64'bz;  // Controlled_Buffer controlled_buffer_14
  assign controlled_buffer_11_out = comparator_51_eq ? sp : 64'bz;  // Controlled_Buffer controlled_buffer_15
  assign controlled_buffer_11_out = comparator_52_eq ? bp : 64'bz;  // Controlled_Buffer controlled_buffer_16
  assign controlled_buffer_11_out = comparator_53_eq ? si : 64'bz;  // Controlled_Buffer controlled_buffer_17
  assign controlled_buffer_11_out = comparator_54_eq ? di : 64'bz;  // Controlled_Buffer controlled_buffer_18
  and and_10 (and_10_out, or_9_out, comparator_35_eq);
  and and_11 (and_11_out, or_10_out, comparator_35_eq);
  and and_12 (and_12_out, or_11_out, comparator_35_eq);
  and and_13 (and_13_out, or_12_out, comparator_35_eq);
  and and_14 (and_14_out, or_13_out, comparator_35_eq);
  and and_15 (and_15_out, or_14_out, comparator_35_eq);
  and and_16 (and_16_out, or_15_out, comparator_35_eq);
  Register #(.width(64)) r8 (.D(multiplexer_9_out), .en(and_10_out), .clk(clk), .Q(eight));  // open: clr
  Multiplexer #(.width(64)) multiplexer_9 (
    .in0(controlled_buffer_1_out), .in1(valM), .out(multiplexer_9_out), .sel(and_1_out));
  Register #(.width(64)) r9 (.D(multiplexer_10_out), .en(and_11_out), .clk(clk), .Q(nine));  // open: clr
  Multiplexer #(.width(64)) multiplexer_10 (
    .in0(controlled_buffer_1_out), .in1(valM), .out(multiplexer_10_out), .sel(and_1_out));
  Register #(.width(64)) r10 (.D(multiplexer_11_out), .en(and_12_out), .clk(clk), .Q(ten));  // open: clr
  Multiplexer #(.width(64)) multiplexer_11 (
    .in0(controlled_buffer_1_out), .in1(valM), .out(multiplexer_11_out), .sel(and_1_out));
  Register #(.width(64)) r11 (.D(multiplexer_12_out), .en(and_13_out), .clk(clk), .Q(elev));  // open: clr
  Multiplexer #(.width(64)) multiplexer_12 (
    .in0(controlled_buffer_1_out), .in1(valM), .out(multiplexer_12_out), .sel(and_1_out));
  Register #(.width(64)) r12 (.D(multiplexer_13_out), .en(and_14_out), .clk(clk), .Q(twel));  // open: clr
  Multiplexer #(.width(64)) multiplexer_13 (
    .in0(controlled_buffer_1_out), .in1(valM), .out(multiplexer_13_out), .sel(and_1_out));
  Register #(.width(64)) r13 (.D(multiplexer_14_out), .en(and_15_out), .clk(clk), .Q(thirt));  // open: clr
  Multiplexer #(.width(64)) multiplexer_14 (
    .in0(controlled_buffer_1_out), .in1(valM), .out(multiplexer_14_out), .sel(and_1_out));
  Register #(.width(64)) r14 (.D(multiplexer_15_out), .en(and_16_out), .Q(fourt));  // open: clk, clr
  Multiplexer #(.width(64)) multiplexer_15 (
    .in0(controlled_buffer_1_out), .in1(valM), .out(multiplexer_15_out), .sel(and_1_out));
  assign controlled_buffer_3_out = comparator_55_eq ? eight : 64'bz;  // Controlled_Buffer controlled_buffer_19
  assign controlled_buffer_3_out = comparator_56_eq ? nine : 64'bz;  // Controlled_Buffer controlled_buffer_20
  assign controlled_buffer_3_out = comparator_57_eq ? ten : 64'bz;  // Controlled_Buffer controlled_buffer_21
  assign controlled_buffer_3_out = comparator_58_eq ? elev : 64'bz;  // Controlled_Buffer controlled_buffer_22
  assign controlled_buffer_3_out = comparator_63_eq ? twel : 64'bz;  // Controlled_Buffer controlled_buffer_23
  assign controlled_buffer_3_out = comparator_64_eq ? thirt : 64'bz;  // Controlled_Buffer controlled_buffer_24
  assign controlled_buffer_3_out = comparator_65_eq ? fourt : 64'bz;  // Controlled_Buffer controlled_buffer_25
  assign controlled_buffer_11_out = comparator_59_eq ? eight : 64'bz;  // Controlled_Buffer controlled_buffer_26
  assign controlled_buffer_11_out = comparator_60_eq ? nine : 64'bz;  // Controlled_Buffer controlled_buffer_27
  assign controlled_buffer_11_out = comparator_61_eq ? ten : 64'bz;  // Controlled_Buffer controlled_buffer_28
  assign controlled_buffer_11_out = comparator_62_eq ? elev : 64'bz;  // Controlled_Buffer controlled_buffer_29
  assign controlled_buffer_11_out = comparator_66_eq ? twel : 64'bz;  // Controlled_Buffer controlled_buffer_30
  assign controlled_buffer_11_out = comparator_67_eq ? thirt : 64'bz;  // Controlled_Buffer controlled_buffer_31
  assign controlled_buffer_11_out = comparator_68_eq ? fourt : 64'bz;  // Controlled_Buffer controlled_buffer_32
  assign controlled_buffer_33_out = not_4_out ? comparator_36_eq : 1'bz;  // Controlled_Buffer controlled_buffer_33
  assign controlled_buffer_34_out = not_5_out ? comparator_36_eq : 1'bz;  // Controlled_Buffer controlled_buffer_34
  Register #(.width(64)) A (
    .D(controlled_buffer_3_out), .en(controlled_buffer_33_out), .clk(clk), .Q(valA));  // open: clr
  Comparator #(.width(4)) comparator_37 (.a(srcA), .b(4'b1111), .eq(comparator_37_eq));  // open: gt, lt
  Register #(.width(64)) B (
    .D(controlled_buffer_11_out), .en(controlled_buffer_34_out), .clk(clk), .Q(valB));  // open: clr
  Comparator #(.width(4)) comparator_38 (.a(srcB), .b(4'b1111), .eq(comparator_38_eq));  // open: gt, lt
  not not_4 (not_4_out, comparator_37_eq);
  not not_5 (not_5_out, comparator_38_eq);
  Comparator #(.width(4)) comparator_39 (.a(srcA), .b(4'b0000), .eq(comparator_39_eq));  // open: gt, lt
  Comparator #(.width(4)) comparator_40 (.a(srcA), .b(4'b0001), .eq(comparator_40_eq));  // open: gt, lt
  Comparator #(.width(4)) comparator_41 (.a(srcA), .b(4'b0010), .eq(comparator_41_eq));  // open: gt, lt
  Comparator #(.width(4)) comparator_42 (.a(srcA), .b(4'b0011), .eq(comparator_42_eq));  // open: gt, lt
  Comparator #(.width(4)) comparator_43 (.a(srcB), .b(4'b0000), .eq(comparator_43_eq));  // open: gt, lt
  Comparator #(.width(4)) comparator_44 (.a(srcB), .b(4'b0001), .eq(comparator_44_eq));  // open: gt, lt
  Comparator #(.width(4)) comparator_45 (.a(srcB), .b(4'b0010), .eq(comparator_45_eq));  // open: gt, lt
  Comparator #(.width(4)) comparator_46 (.a(srcB), .b(4'b0011), .eq(comparator_46_eq));  // open: gt, lt
  Comparator #(.width(4)) comparator_47 (.a(srcA), .b(4'b0100), .eq(comparator_47_eq));  // open: gt, lt
  Comparator #(.width(4)) comparator_48 (.a(srcA), .b(4'b0101), .eq(comparator_48_eq));  // open: gt, lt
  Comparator #(.width(4)) comparator_49 (.a(srcA), .b(4'b0110), .eq(comparator_49_eq));  // open: gt, lt
  Comparator #(.width(4)) comparator_50 (.a(srcA), .b(4'b0111), .eq(comparator_50_eq));  // open: gt, lt
  Comparator #(.width(4)) comparator_51 (.a(srcB), .b(4'b0100), .eq(comparator_51_eq));  // open: gt, lt
  Comparator #(.width(4)) comparator_52 (.a(srcB), .b(4'b0101), .eq(comparator_52_eq));  // open: gt, lt
  Comparator #(.width(4)) comparator_53 (.a(srcB), .b(4'b0110), .eq(comparator_53_eq));  // open: gt, lt
  Comparator #(.width(4)) comparator_54 (.a(srcB), .b(4'b0111), .eq(comparator_54_eq));  // open: gt, lt
  Comparator #(.width(4)) comparator_55 (.a(srcA), .b(4'b1000), .eq(comparator_55_eq));  // open: gt, lt
  Comparator #(.width(4)) comparator_56 (.a(srcA), .b(4'b1001), .eq(comparator_56_eq));  // open: gt, lt
  Comparator #(.width(4)) comparator_57 (.a(srcA), .b(4'b1010), .eq(comparator_57_eq));  // open: gt, lt
  Comparator #(.width(4)) comparator_58 (.a(srcA), .b(4'b1011), .eq(comparator_58_eq));  // open: gt, lt
  Comparator #(.width(4)) comparator_59 (.a(srcB), .b(4'b1000), .eq(comparator_59_eq));  // open: gt, lt
  Comparator #(.width(4)) comparator_60 (.a(srcB), .b(4'b1001), .eq(comparator_60_eq));  // open: gt, lt
  Comparator #(.width(4)) comparator_61 (.a(srcB), .b(4'b1010), .eq(comparator_61_eq));  // open: gt, lt
  Comparator #(.width(4)) comparator_62 (.a(srcB), .b(4'b1011), .eq(comparator_62_eq));  // open: gt, lt
  Comparator #(.width(4)) comparator_63 (.a(srcA), .b(4'b1100), .eq(comparator_63_eq));  // open: gt, lt
  Comparator #(.width(4)) comparator_64 (.a(srcA), .b(4'b1101), .eq(comparator_64_eq));  // open: gt, lt
  Comparator #(.width(4)) comparator_65 (.a(srcA), .b(4'b1110), .eq(comparator_65_eq));  // open: gt, lt
  Comparator #(.width(4)) comparator_66 (.a(srcB), .b(4'b1100), .eq(comparator_66_eq));  // open: gt, lt
  Comparator #(.width(4)) comparator_67 (.a(srcB), .b(4'b1101), .eq(comparator_67_eq));  // open: gt, lt
  Comparator #(.width(4)) comparator_68 (.a(srcB), .b(4'b1110), .eq(comparator_68_eq));  // open: gt, lt
endmodule

module Memory (
  input  [3:0] icode,
  input  [63:0] valE,
  input  [63:0] valA,
  input  [11:0] valP,
  input  clk,
  input  [7:0] cyc,
  output [63:0] valM
);

  wire and_1_out, and_2_out, and_3_out, and_4_out, and_5_out, and_6_out, and_7_out, and_8_out, and_9_out,
       and_10_out, and_11_out, comparator_1_eq, comparator_2_eq, comparator_3_eq, comparator_4_eq,
       comparator_5_eq, comparator_6_eq, comparator_7_eq, comparator_7_gt, comparator_8_lt, comparator_9_eq,
       comparator_10_eq, comparator_11_eq, comparator_12_eq, comparator_13_eq, comparator_14_eq,
       comparator_15_eq, comparator_16_eq, comparator_17_eq, or_1_out, or_2_out;
  wire [7:0] controlled_buffer_1_out, multiplexer_2_out, multiplexer_2_out_2, multiplexer_2_out_3,
       multiplexer_2_out_4, multiplexer_2_out_5, multiplexer_2_out_6, multiplexer_2_out_7,
       multiplexer_2_out_8, ram_1_dout;
  wire [11:0] address_q, multiplexer_1_out;

  Comparator #(.width(4)) comparator_1 (.a(icode), .b(4'b1010), .eq(comparator_1_eq));  // open: gt, lt
  Comparator #(.width(4)) comparator_2 (.a(icode), .b(4'b1000), .eq(comparator_2_eq));  // open: gt, lt
  Comparator #(.width(4)) comparator_3 (.a(icode), .b(4'b0100), .eq(comparator_3_eq));  // open: gt, lt
  Comparator #(.width(4)) comparator_4 (.a(icode), .b(4'b1011), .eq(comparator_4_eq));  // open: gt, lt
  Comparator #(.width(4)) comparator_5 (.a(icode), .b(4'b1001), .eq(comparator_5_eq));  // open: gt, lt
  Comparator #(.width(4)) comparator_6 (.a(icode), .b(4'b0101), .eq(comparator_6_eq));  // open: gt, lt
  Comparator comparator_7 (.a(cyc), .b(8'hb), .gt(comparator_7_gt), .eq(comparator_7_eq));  // open: lt
  Comparator comparator_8 (.a(cyc), .b(8'h14), .lt(comparator_8_lt));  // open: gt, eq
  Multiplexer #(.select(4), .width(12)) multiplexer_1 (
    .in4(valE[11:0]), .in5(valE[11:0]), .in8(valE[11:0]), .in9(valA[11:0]), .in10(valE[11:0]),
    .in11(valA[11:0]), .out(multiplexer_1_out), .sel(icode));  // open: in0, in1, in2, in3, in6, in7, in12, in13, in14, in15
  Multiplexer #(.select(4), .width(64)) multiplexer_2 (
    .in4(valA), .in8({{52{1'b0}}, valP}), .in10(valA),
    .out({multiplexer_2_out_8, multiplexer_2_out_7, multiplexer_2_out_6, multiplexer_2_out_5, multiplexer_2_out_4, multiplexer_2_out_3, multiplexer_2_out_2, multiplexer_2_out}),
    .sel(icode));  // open: in0, in1, in2, in3, in5, in6, in7, in9, in11, in12, in13, in14, in15
  or or_1 (or_1_out, comparator_1_eq, comparator_2_eq, comparator_3_eq);
  or or_2 (or_2_out, comparator_4_eq, comparator_5_eq, comparator_6_eq);
  and and_1 (and_1_out, comparator_7_gt, comparator_8_lt);
  and and_2 (and_2_out, or_1_out, and_1_out);
  and and_3 (and_3_out, or_2_out, and_1_out);
  assign controlled_buffer_1_out = comparator_9_eq ? multiplexer_2_out : 8'bz;  // Controlled_Buffer controlled_buffer_1
  Comparator comparator_9 (.a(cyc), .b(8'hc), .eq(comparator_9_eq));  // open: gt, lt
  assign controlled_buffer_1_out = comparator_10_eq ? multiplexer_2_out_2 : 8'bz;  // Controlled_Buffer controlled_buffer_2
  assign controlled_buffer_1_out = comparator_11_eq ? multiplexer_2_out_3 : 8'bz;  // Controlled_Buffer controlled_buffer_3
  assign controlled_buffer_1_out = comparator_12_eq ? multiplexer_2_out_4 : 8'bz;  // Controlled_Buffer controlled_buffer_4
  Comparator comparator_10 (.a(cyc), .b(8'hd), .eq(comparator_10_eq));  // open: gt, lt
  assign controlled_buffer_1_out = comparator_13_eq ? multiplexer_2_out_5 : 8'bz;  // Controlled_Buffer controlled_buffer_5
  assign controlled_buffer_1_out = comparator_14_eq ? multiplexer_2_out_6 : 8'bz;  // Controlled_Buffer controlled_buffer_6
  assign controlled_buffer_1_out = comparator_15_eq ? multiplexer_2_out_7 : 8'bz;  // Controlled_Buffer controlled_buffer_7
  and and_4 (and_4_out, comparator_10_eq, or_2_out);
  Counter #(.max('hfff), .width(12)) address (
    .load(comparator_7_eq), .count(and_1_out), .clk(clk), .D(multiplexer_1_out), .Q(address_q));  // open: clr, up, carry
  assign controlled_buffer_1_out = comparator_16_eq ? multiplexer_2_out_8 : 8'bz;  // Controlled_Buffer controlled_buffer_8
  Comparator comparator_11 (.a(cyc), .b(8'he), .eq(comparator_11_eq));  // open: gt, lt
  Comparator comparator_12 (.a(cyc), .b(8'hf), .eq(comparator_12_eq));  // open: gt, lt
  and and_5 (and_5_out, comparator_11_eq, or_2_out);
  Comparator comparator_13 (.a(cyc), .b(8'h10), .eq(comparator_13_eq));  // open: gt, lt
  and and_6 (and_6_out, comparator_12_eq, or_2_out);
  and and_7 (and_7_out, comparator_13_eq, or_2_out);
  Comparator comparator_14 (.a(cyc), .b(8'h11), .eq(comparator_14_eq));  // open: gt, lt
  RAM #(.addrWidth(12)) ram_1 (
    .addr(address_q), .we(and_2_out), .oe(and_3_out), .clk(clk), .din(controlled_buffer_1_out),
    .dout(ram_1_dout));
  Comparator comparator_15 (.a(cyc), .b(8'h12), .eq(comparator_15_eq));  // open: gt, lt
  and and_8 (and_8_out, comparator_14_eq, or_2_out);
  Comparator comparator_16 (.a(cyc), .b(8'h13), .eq(comparator_16_eq));  // open: gt, lt
  and and_9 (and_9_out, comparator_15_eq, or_2_out);
  and and_10 (and_10_out, comparator_16_eq, or_2_out);
  Comparator comparator_17 (.a(cyc), .b(8'h14), .eq(comparator_17_eq));  // open: gt, lt
  and and_11 (and_11_out, comparator_17_eq, or_2_out);
  Register register_1 (.D(ram_1_dout), .en(and_4_out), .clk(clk), .Q(valM[7:0]));  // open: clr
  Register register_2 (.D(ram_1_dout), .en(and_5_out), .clk(clk), .Q(valM[15:8]));  // open: clr
  Register register_3 (.D(ram_1_dout), .en(and_6_out), .clk(clk), .Q(valM[23:16]));  // open: clr
  Register register_4 (.D(ram_1_dout), .en(and_7_out), .clk(clk), .Q(valM[31:24]));  // open: clr
  Register register_5 (.D(ram_1_dout), .en(and_8_out), .clk(clk), .Q(valM[39:32]));  // open: clr
  Register register_6 (.D(ram_1_dout), .en(and_9_out), .clk(clk), .Q(valM[47:40]));  // open: clr
  Register register_7 (.D(ram_1_dout), .en(and_10_out), .clk(clk), .Q(valM[55:48]));  // open: clr
  Register register_8 (.D(ram_1_dout), .en(and_11_out), .clk(clk), .Q(valM[63:56]));  // open: clr
endmodule
